// Digital circuit cpu_2.dig as structural Verilog
module cpu_2 (
);

  wire _74574_1_pin1, _74574_1_pin11, _74574_2_pin2, _74574_2_pin3, _74574_2_pin4, _74574_2_pin5,
       _74574_2_pin6, _74574_2_pin7, _74574_2_pin8, _74574_2_pin9, _74574_3_pin2, _74574_3_pin3,
       _74574_3_pin4, _74574_3_pin5, _74574_3_pin6, _74574_3_pin7, _74574_3_pin8, _74574_3_pin9,
       _74574_4_pin2, _74574_4_pin3, _74574_4_pin4, _74574_4_pin5, _74574_4_pin6, _74574_4_pin7,
       _74574_4_pin8, _74574_4_pin9;
  wire [7:0] _74574_1_pin2;
  wire [31:0] _74574_1_pin19;

  _74574 _74574_1 (
    .pin1(_74574_1_pin1), .pin2(_74574_1_pin2[0]), .pin3(_74574_1_pin2[1]), .pin4(_74574_1_pin2[2]),
    .pin5(_74574_1_pin2[3]), .pin6(_74574_1_pin2[4]), .pin7(_74574_1_pin2[5]), .pin8(_74574_1_pin2[6]),
    .pin9(_74574_1_pin2[7]), .pin10(1'b0), .pin11(_74574_1_pin11), .pin12(_74574_1_pin19[7]),
    .pin13(_74574_1_pin19[6]), .pin14(_74574_1_pin19[5]), .pin15(_74574_1_pin19[4]),
    .pin16(_74574_1_pin19[3]), .pin17(_74574_1_pin19[2]), .pin18(_74574_1_pin19[1]),
    .pin19(_74574_1_pin19[0]), .pin20(1'b1));
  _74574 _74574_2 (
    .pin1(_74574_1_pin1), .pin2(_74574_2_pin2), .pin3(_74574_2_pin3), .pin4(_74574_2_pin4),
    .pin5(_74574_2_pin5), .pin6(_74574_2_pin6), .pin7(_74574_2_pin7), .pin8(_74574_2_pin8),
    .pin9(_74574_2_pin9), .pin10(1'b0), .pin11(_74574_1_pin11), .pin12(_74574_1_pin19[15]),
    .pin13(_74574_1_pin19[14]), .pin14(_74574_1_pin19[13]), .pin15(_74574_1_pin19[12]),
    .pin16(_74574_1_pin19[11]), .pin17(_74574_1_pin19[10]), .pin18(_74574_1_pin19[9]),
    .pin19(_74574_1_pin19[8]), .pin20(1'b1));
  _74574 _74574_3 (
    .pin1(_74574_1_pin1), .pin2(_74574_3_pin2), .pin3(_74574_3_pin3), .pin4(_74574_3_pin4),
    .pin5(_74574_3_pin5), .pin6(_74574_3_pin6), .pin7(_74574_3_pin7), .pin8(_74574_3_pin8),
    .pin9(_74574_3_pin9), .pin10(1'b0), .pin11(_74574_1_pin11), .pin12(_74574_1_pin19[23]),
    .pin13(_74574_1_pin19[22]), .pin14(_74574_1_pin19[21]), .pin15(_74574_1_pin19[20]),
    .pin16(_74574_1_pin19[19]), .pin17(_74574_1_pin19[18]), .pin18(_74574_1_pin19[17]),
    .pin19(_74574_1_pin19[16]), .pin20(1'b1));
  _74574 _74574_4 (
    .pin1(_74574_1_pin1), .pin2(_74574_4_pin2), .pin3(_74574_4_pin3), .pin4(_74574_4_pin4),
    .pin5(_74574_4_pin5), .pin6(_74574_4_pin6), .pin7(_74574_4_pin7), .pin8(_74574_4_pin8),
    .pin9(_74574_4_pin9), .pin10(1'b0), .pin11(_74574_1_pin11), .pin12(_74574_1_pin19[31]),
    .pin13(_74574_1_pin19[30]), .pin14(_74574_1_pin19[29]), .pin15(_74574_1_pin19[28]),
    .pin16(_74574_1_pin19[27]), .pin17(_74574_1_pin19[26]), .pin18(_74574_1_pin19[25]),
    .pin19(_74574_1_pin19[24]), .pin20(1'b1));
endmodule
